# Fritzing sketch breadboard (saved by Fritzing 0.9.6b)
breadboards: 3

parts:
  S3 = Pushbutton [package="[THT]"]
  S4 = Pushbutton [package="[THT]"]
  S5 = Pushbutton [package="[THT]"]
  C1 = Capacitor [package=cap-pth-small2]
  R1 = Resistor [tolerance=±5% resistance=1k power=0.25 package=THT]
  U1 = CD4013BE [part_number=CD4013BE package="DIP (Dual Inline) [THT]"]
  Part1 = CD4013BE [part_number=CD4013BE package="DIP (Dual Inline) [THT]"]  # not connected
  U1_1 = CD4013BE [part_number=CD4013BE package="DIP (Dual Inline) [THT]"]  # not connected
  U1_2 = CD4013BE [part_number=CD4013BE package="DIP (Dual Inline) [THT]"]  # not connected
  U1_3 = CD4013BE [part_number=CD4013BE package="DIP (Dual Inline) [THT]"]  # not connected
  U1_4 = CD4013BE [part_number=CD4013BE package="DIP (Dual Inline) [THT]"]  # not connected
  R2 = Resistor [tolerance=±5% resistance=1k power=0.25 package=THT]
  C2 = Capacitor [package=cap-pth-small2]
  U2 = 555 Timer [package="DIP8 [THT]"]
  IC1 = CD40110BE [package="DIP16 [THT]"]
  7_Segment2 = 7 Segment Display
  R10 = Resistor [tolerance=±5% resistance=10k power=0.25 package=THT]
  R11 = Resistor [tolerance=±5% resistance=10k power=0.25 package=THT]
  C5 = Capacitor [package=cap-pth-small2]
  C6 = Capacitor [package=cap-pth-small2]
  D1 = Rectifier Diode 10A [part_number=P1000K]
  R12 = Resistor [tolerance=±5% resistance=10k power=0.25 package=THT]
  R13 = Resistor [tolerance=±5% resistance=10k power=0.25 package=THT]
  U3 = 555 Timer [package="DIP8 [THT]"]
  D2 = Rectifier Diode 10A [part_number=P1000K]
  C7 = Capacitor [package=cap-pth-small2]
  R14 = Resistor [tolerance=±5% resistance=10k power=0.25 package=THT]
  C8 = Capacitor [package=cap-pth-small2]
  D3 = Rectifier Diode 10A [part_number=P1000K]  # not connected

nets:
  N1: S3.Pin_1, S3.Pin_2, C1.2, C2.1
  N2: S3.Pin_3, S3.Pin_4, C1.1, R1.Pin_0, U1.connector2, D2.cathode
  N3: S4.Pin_1, S4.Pin_2, S5.Pin_1, S5.Pin_2
  N4: S4.Pin_3, S4.Pin_4, IC1.COM_-_Common, IC1.Out_3, 7_Segment2.Segment_C, R13.Pin_1
  N5: S5.Pin_3, S5.Pin_4, IC1.In_2, IC1.In_7, 7_Segment2.Segment_G, D1.cathode, R12.Pin_0
  N6: R1.Pin_1, U1.connector5, U1.connector6, R2.Pin_1, U2.Ground, IC1.In_4, IC1.In_5, IC1.In_6, IC1.0V, R12.Pin_1, U3.Ground
  N7: U1.connector1, U1.connector4, U2.Vcc_Supply_Voltage, R10.Pin_0
  N8: U1.connector3, R2.Pin_0, C2.2
  N9: U1.connector7, U1.connector9, U1.connector10, U1.connector11, U1.connector12, IC1.Out_7, C6.1, R13.Pin_0, C7.1, C8.1
  N10: U1.connector13, IC1.Out_1, U3.Vcc_Supply_Voltage, R14.Pin_1
  N11: U2.Trigger, U2.Threshold, R11.Pin_0, C5.2
  N12: U2.Output, D1.anode
  N13: U2.Control_Voltage, C6.2
  N14: U2.Discharge, R10.Pin_1, R11.Pin_1
  N15: IC1.In_1, 7_Segment2.Segment_A
  N16: IC1.In_3, 7_Segment2.Segment_F
  N17: IC1.Out_6, IC1.Out_2, 7_Segment2.Segment_B, U3.Trigger
  N18: IC1.Out_5, 7_Segment2.Segment_E
  N19: IC1.Out_4, 7_Segment2.Segment_D
  N20: 7_Segment2.common_cathode, C5.1
  N21: U3.Output, D2.anode
  N22: U3.Control_Voltage, C7.2
  N23: U3.Threshold, U3.Discharge, R14.Pin_0, C8.2

notes:
  Start/Stop
  Up
  Down

custom parts:
  CD4013BE: 4071 4 x 2 Input OR Gate with sub-parts
  CD4013BE: 4071 4 x 2 Input OR Gate with sub-parts
  CD4013BE: 4071 4 x 2 Input OR Gate with sub-parts
  CD4013BE: 4071 4 x 2 Input OR Gate with sub-parts
  CD4013BE: 4071 4 x 2 Input OR Gate with sub-parts
  CD4013BE: 4071 4 x 2 Input OR Gate with sub-parts
  CD40110BE: ULN2003A 7-way Darlington Transistor Driver
